// Logisim project 4laba.circ as structural Verilog: 1 circuit, main circuit main
module main (
  input  in_1,
  input  in_2,
  input  in_3,
  input  in_4,
  input  in_5,
  input  in_6,
  input  in_7,
  input  in_8,
  input  in_9,
  input  in_10,
  input  in_11,
  input  in_12,
  input  in_13,
  output out_14,
  output out_15,
  output out_16,
  output out_17,
  output out_18,
  output out_19,
  output out_20,
  output out_21,
  output out_22,
  output out_23,
  output out_24,
  output out_25
);

  wire nand_1_out, nand_2_out, nand_3_out, nand_4_out, nand_5_out, nand_6_out, nand_7_out, nand_8_out,
       nand_11_out, nand_12_out;

  nand nand_1 (nand_1_out, in_5, in_6);
  nand nand_2 (nand_2_out, in_6, in_7);
  nand nand_3 (nand_3_out, in_8, in_8);
  nand nand_4 (nand_4_out, nand_3_out, in_9);
  nand nand_5 (nand_5_out, in_10, nand_6_out);
  nand nand_6 (nand_6_out, in_11, in_11);
  nand nand_7 (nand_7_out, in_12, in_12);
  nand nand_8 (nand_8_out, in_13, in_13);
  nor nor_1 (out_14, in_1, out_15);
  nor nor_2 (out_15, out_14, in_2);
  nand nand_9 (out_16, in_3, out_17);
  nand nand_10 (out_17, out_16, in_4);
  nand nand_11 (nand_11_out, in_12, nand_8_out);
  nand nand_12 (nand_12_out, nand_7_out, in_13);
  nand nand_13 (out_18, nand_1_out, out_19);
  nand nand_14 (out_19, out_18, nand_2_out);
  nand nand_15 (out_20, nand_3_out, out_21);
  nand nand_16 (out_21, out_20, nand_4_out);
  nand nand_17 (out_22, nand_5_out, out_23);
  nand nand_18 (out_23, out_22, nand_6_out);
  nand nand_19 (out_24, nand_11_out, out_25);
  nand nand_20 (out_25, out_24, nand_12_out);

  // Notes on the sheet:
  //   Асинхронный RS триггер с прямыми входами
  //   Синхронный RS триггер
  //   S-триггер
  //   R-триггер
  //   E-триггер
  //   Асинхронный RS триггер с инверсными входами
endmodule
