// Logisim project laba6.circ as structural Verilog: 6 circuits, main circuit Схема сравнения
module \Схема_сравнения  (
  input  X1,
  input  x2,
  output y
);

  wire and_1_out, and_2_out, not_1_out, not_2_out;

  not not_1 (not_1_out, X1);
  not not_2 (not_2_out, x2);
  and and_1 (and_1_out, not_1_out, x2);
  and and_2 (and_2_out, X1, not_2_out);
  or or_1 (y, and_1_out, and_2_out);

  // Notes on the sheet:
  //   Схема сравнения
endmodule

module \Полусумматор  (
  input  in_1,
  input  in_2,
  output out_3,
  output out_4
);

  \Схема_сравнения  \u_схема_сравнения_1  (.X1(in_1), .x2(in_2), .y(out_4));
  and \u_и  (out_3, in_1, in_2);

  // Notes on the sheet:
  //   Полусумматор
  //   Схема сравнения
endmodule

module \Полный_сумматор  (
  input  x1,
  input  x2,
  input  pi,
  output P,
  output S
);

  wire \полусумматор_1_out_3 , \полусумматор_1_out_4 , \полусумматор_2_out_3 ;

  \Полусумматор  \u_полусумматор_1  (
    .in_1(x1), .in_2(x2), .out_3(\полусумматор_1_out_3 ), .out_4(\полусумматор_1_out_4 ));
  \Полусумматор  \u_полусумматор_2  (
    .in_1(\полусумматор_1_out_4 ), .in_2(pi), .out_3(\полусумматор_2_out_3 ), .out_4(S));
  or \u_или  (P, \полусумматор_1_out_3 , \полусумматор_2_out_3 );

  // Notes on the sheet:
  //   Полусумматор
  //   Сумматор
  //   Полусумматор
endmodule

module \_4_сумматора  (
  input  x4,
  input  y4,
  input  x3,
  input  y3,
  input  x2,
  input  Y2,
  input  x1,
  input  y1,
  input  P0,
  output P4,
  output out_11,
  output out_12,
  output out_13,
  output out_14
);

  wire \полный_сумматор_1_p , \полный_сумматор_2_p , \полный_сумматор_3_p ;

  \Полный_сумматор  \u_полный_сумматор_1  (.x1(x1), .x2(y1), .pi(P0), .P(\полный_сумматор_1_p ), .S(out_14));
  \Полный_сумматор  \u_полный_сумматор_2  (
    .x1(x2), .x2(Y2), .pi(\полный_сумматор_1_p ), .P(\полный_сумматор_2_p ), .S(out_13));
  \Полный_сумматор  \u_полный_сумматор_3  (
    .x1(x3), .x2(y3), .pi(\полный_сумматор_2_p ), .P(\полный_сумматор_3_p ), .S(out_12));
  \Полный_сумматор  \u_полный_сумматор_4  (.x1(x4), .x2(y4), .pi(\полный_сумматор_3_p ), .P(P4), .S(out_11));

  // Notes on the sheet:
  //   P1
  //   P2
  //   P3
endmodule

module \полусумматор_теория  (
  input  A,
  input  B,
  output S,
  output P
);

  wire not_1_out, or_1_out;

  or or_1 (or_1_out, A, B);
  and and_1 (P, A, B);
  not not_1 (not_1_out, P);
  and and_2 (S, or_1_out, not_1_out);

  // Notes on the sheet:
  //   Полусумматор теория
endmodule

module \полный_сумматор_теория  (
  input  A,
  input  B,
  input  P0,
  output P,
  output S
);

  wire and_1_out, and_2_out, and_3_out, and_4_out, and_5_out, not_1_out, or_1_out;

  and and_1 (and_1_out, A, B);
  and and_2 (and_2_out, A, P0);
  and and_3 (and_3_out, B, P0);
  or or_1 (or_1_out, A, B, P0);
  and and_4 (and_4_out, A, B, P0);
  or or_2 (P, and_1_out, and_2_out, and_3_out);
  not not_1 (not_1_out, P);
  and and_5 (and_5_out, not_1_out, or_1_out);
  or or_3 (S, and_5_out, and_4_out);

  // Notes on the sheet:
  //   Полный сумматор теория
endmodule
